# Fritzing sketch simon (saved by Fritzing 0.9.3b)
breadboards: 1

parts:
  Part1 = Arduino Uno (Rev3)
  LED1 = LED - 5mm [color="Blue (525nm)" package="5 mm [THT]"]
  LED2 = LED - 5mm [color="Yellow (585nm)" package="5 mm [THT]"]
  R1 = Resistor [tolerance=±5% resistance=220 package=THT]
  R2 = Resistor [tolerance=±5% resistance=220 package=THT]
  LED3 = LED - 5mm [color="Red (660nm)" package="5 mm [THT]"]
  LED4 = LED - 5mm [color="Green (555nm)" package="5 mm [THT]"]
  R3 = Resistor [tolerance=±5% resistance=220 package=THT]
  R4 = Resistor [tolerance=±5% resistance=220 package=THT]
  S1 = Pushbutton [package="[THT]"]
  S2 = Pushbutton [package="[THT]"]
  S3 = Pushbutton [package="[THT]"]
  S4 = Pushbutton [package="[THT]"]
  R5 = Resistor [tolerance=±5% resistance=220 package=THT]
  R6 = Resistor [tolerance=±5% resistance=220 package=THT]
  R7 = Resistor [tolerance=±5% resistance=220 package=THT]
  R8 = Resistor [tolerance=±5% resistance=220 package=THT]
  J1 = Piezo Speaker

nets:
  N1: Part1.A0, S1.Pin_3, S1.Pin_4, R5.Pin_1
  N2: Part1.A1, S2.Pin_3, S2.Pin_4, R6.Pin_1
  N3: Part1.A2, S3.Pin_3, S3.Pin_4, R7.Pin_1
  N4: Part1.A3, S4.Pin_3, S4.Pin_4, R8.Pin_1
  N5: Part1.D8, J1.pin2
  N6: Part1.D2, R4.Pin_1
  N7: Part1.D3_PWM, R3.Pin_1
  N8: Part1.D4, R2.Pin_1
  N9: Part1.D5_PWM, R1.Pin_1
  N10: Part1.5V, R5.Pin_0, R6.Pin_0, R7.Pin_0, R8.Pin_0
  N11: Part1.GND, LED1.cathode, LED2.cathode, LED3.cathode, LED4.cathode, S1.Pin_1, S1.Pin_2, S2.Pin_1, S2.Pin_2, S3.Pin_1, S3.Pin_2, S4.Pin_1, S4.Pin_2, J1.pin1
  N12: LED1.anode, R1.Pin_0
  N13: LED2.anode, R2.Pin_0
  N14: LED3.anode, R3.Pin_0
  N15: LED4.anode, R4.Pin_0
